# Fritzing sketch dc-mouse (saved by Fritzing 0.9.2b)
breadboards: 1

parts:
  PC = 4 x AAA Battery Mount
  Mouse = Pushbutton [package=THT]
  EEGDC1 = Resistor [tolerance=±0.05% resistance=100 package=THT]
  Proteção = Resistor [tolerance=±2% resistance=680 package="0603 [SMD]"]

nets:
  GND: PC.-, Mouse.leg0, EEGDC1.Pin_1
  N1: PC.+, Mouse.leg1, Proteção.Pin_1
  N2: EEGDC1.Pin_0, Proteção.Pin_0
