# Fritzing sketch dc-mouse (saved by Fritzing 0.9.2b)
breadboards: 1

parts:
  PC = 4 x AAA Battery Mount
  EEGDC1 = Resistor [tolerance=±0.05% resistance=100 package=THT]
  Mouse = Pushbutton [package="[THT]"]
  Mouse_Proctection = Resistor [tolerance=±5% resistance=220 package=THT]
  Protection = Resistor [tolerance=±2% resistance=470 package=THT]
  BJTR = Resistor [tolerance=±5% resistance=100 package=THT]
  NPN = npn-Powertransistor [package="TO220 [THT]"]
  R1 = Resistor [tolerance=±5% resistance=220 package=THT]

nets:
  GND: PC.-, EEGDC1.Pin_1, NPN.emitter
  N1: PC.+, Mouse_Proctection.Pin_0
  N2: EEGDC1.Pin_0, Protection.Pin_1
  N3: Mouse.Pin_1, Mouse.Pin_2, BJTR.Pin_0
  N4: Mouse.Pin_3, Mouse.Pin_4, Mouse_Proctection.Pin_1, R1.Pin_0
  N5: Protection.Pin_0, NPN.collector, R1.Pin_1
  N6: BJTR.Pin_1, NPN.base
